# Fritzing sketch board (saved by Fritzing 0.9.0b)
circuit board: 8.13cm x 7.64cm
breadboards: 1

parts:
  LED1 = LED - 5mm [color="Green (570nm)" package="5 mm [THT]"]
  LED2 = LED - 5mm [color="Green (570nm)" package="5 mm [THT]"]
  LED3 = LED - 5mm [color="Green (570nm)" package="5 mm [THT]"]
  LED4 = LED - 5mm [color="Green (570nm)" package="5 mm [THT]"]
  LED7 = LED - 5mm [color="Green (570nm)" package="5 mm [THT]"]
  LED8 = LED - 5mm [color="Green (570nm)" package="5 mm [THT]"]
  LED9 = LED - 5mm [color="Green (570nm)" package="5 mm [THT]"]
  LED10 = LED - 5mm [color="Green (570nm)" package="5 mm [THT]"]
  LED11 = LED - 5mm [color="Green (570nm)" package="5 mm [THT]"]
  LED12 = LED - 5mm [color="Green (570nm)" package="5 mm [THT]"]
  LED13 = LED - 5mm [color="Green (570nm)" package="5 mm [THT]"]
  LED14 = LED - 5mm [color="Green (570nm)" package="5 mm [THT]"]
  LED15 = LED - 5mm [color="Green (570nm)" package="5 mm [THT]"]
  LED16 = LED - 5mm [color="Green (570nm)" package="5 mm [THT]"]
  74HC595 = 74HC595 [package="DIP16 [THT]"]
  ATTiny = attiny85 [package=dip]
  U18 = Voltage Regulator - 5V [package="TO220 [THT]"]
  Power = Battery block 9V
  Right = Pushbutton [package=THT]
  Left = Pushbutton [package=THT]
  R1 = Resistor [tolerance=±5% resistance=220 package=THT]
  R2 = Resistor [tolerance=±5% resistance=220 package=THT]
  R3 = Resistor [tolerance=±5% resistance=220 package=THT]
  R4 = Resistor [tolerance=±5% resistance=220 package=THT]
  R5 = Resistor [tolerance=±5% resistance=220 package=THT]
  R6 = Resistor [tolerance=±5% resistance=220 package=THT]
  R7 = Resistor [tolerance=±5% resistance=220 package=THT]
  R8 = Resistor [tolerance=±5% resistance=220 package=THT]
  R9 = Resistor [tolerance=±5% resistance=10k package=THT]
  R11 = Resistor [tolerance=±5% resistance=10k package=THT]

nets:
  GND: LED1.cathode, LED2.cathode, LED3.cathode, LED4.cathode, LED7.cathode, LED8.cathode, LED9.cathode, LED10.cathode, LED11.cathode, LED12.cathode, LED13.cathode, LED14.cathode, LED15.cathode, LED16.cathode, 74HC595.GND, 74HC595.OE, ATTiny.Pin_4, U18.GND, Power.-, R9.Pin_0, R11.Pin_0
  N1: LED1.anode, LED8.anode, R4.Pin_1
  N2: LED2.anode, LED9.anode, R1.Pin_1
  N3: LED3.anode, LED7.anode, R5.Pin_1
  N4: LED4.anode, R6.Pin_1
  N5: LED10.anode, R2.Pin_1
  N6: LED11.anode, LED15.anode, R8.Pin_1
  N7: LED12.anode, LED14.anode, 74HC595.Q2, R3.Pin_0, R3.Pin_1
  N8: LED13.anode, LED16.anode, R7.Pin_1
  N9: 74HC595.Q1, R8.Pin_0
  N10: 74HC595.Q3, R7.Pin_0
  N11: 74HC595.Q4, R5.Pin_0
  N12: 74HC595.Q5, R1.Pin_0
  N13: 74HC595.Q6, R4.Pin_0
  N14: 74HC595.Q7, R6.Pin_0
  N15: 74HC595.MR, 74HC595.VCC, ATTiny.Pin_8, U18.input_voltage, Right.leg0, Left.leg0
  N16: 74HC595.SH_CP, ATTiny.Pin_2
  N17: 74HC595.ST_CP, ATTiny.Pin_3
  N18: 74HC595.DS, ATTiny.Pin_7
  N19: 74HC595.Q0, R2.Pin_0
  N20: ATTiny.Pin_5, Right.leg1, R9.Pin_1
  N21: ATTiny.Pin_6, Left.leg1, R11.Pin_1
  N22: U18.output_voltage, Power.+

notes:
  Knowledge And Technology Joyfully Engaged
  W.A. ten Brink
